# Fritzing sketch sbrn_attyny85 (saved by Fritzing 0.9.2b)
circuit board: 8.00001cm x 8.00001cm
breadboards: 1

parts:
  Core = attiny85 [package=dip]
  Disparador = Audio Jack (TRS) 3.5mm [package="PG203J [THT]"]
  IR1 = TSOP312.., 314.. [package=THT]
  pot = Rotary Potentiometer (Large) [maximum_resistance=100kΩ package=THT]
  Indicador = LED - 5mm [color="Red (633nm)" package="5 mm [THT]"]
  12v = 2.1mm DC Barrel Jack
  5v = Voltage Regulator [package=78xxl]
  Tip120_Red = TIP120 Hi-Current Darlington Transistor
  Tip120_Key = TIP120 Hi-Current Darlington Transistor
  D1 = Rectifier Diode [part_number=1N4001 package="Melf DO-213 AB [SMD]"]
  D2 = Rectifier Diode [part_number=1N4001 package="Melf DO-213 AB [SMD]"]
  Red = Luxeon LED [package=luxeon]
  U1 = Luxeon LED [package=luxeon]
  R2 = Resistor [tolerance=±20% resistance=330 package=THT]
  R1 = Resistor [tolerance=±5% resistance=330 package=THT]
  R3 = Resistor [tolerance=±5% resistance=10k package=THT]

nets:
  N1: Core.Pin_2, IR1.Data
  N2: Core.Pin_3, Disparador.Ring, Disparador.Tip, R3.Pin_0
  GND: Core.Pin_4, IR1.GND, pot.leg2, 12v.sleeve, 5v.GND, Tip120_Red.EMITTER, Tip120_Key.EMITTER, D1.anode, D2.anode, R3.Pin_1
  N3: Core.Pin_5, R2.Pin_0
  N4: Core.Pin_6, R1.Pin_0
  N5: Core.Pin_7, pot.wiper
  N6: Core.Pin_8, Disparador.Sleeve, IR1.Vs, pot.leg1, Indicador.anode, 5v.OUT, Red.A
  N7: Indicador.cathode, Tip120_Key.BASE, R1.Pin_1
  N8: 12v.center, 5v.IN, U1.A
  N9: Tip120_Red.BASE, R2.Pin_1
  N10: Tip120_Red.COLLECTOR, D2.cathode, Red.C
  N11: Tip120_Key.COLLECTOR, D1.cathode, U1.C

custom parts:
  2.1mm DC Barrel Jack: 2.1mm DC Barrel Jack with Thru-Hole Connectors (breadboardable)

// code stored in the sketch: Untitled.ino

